# Fritzing sketch dc-mouse (saved by Fritzing 0.9.2b)
breadboards: 1

parts:
  PC = 4 x AAA Battery Mount
  EEGDC1 = Resistor [tolerance=±0.05% resistance=100 package=THT]
  Mouse = Pushbutton [package="[THT]"]
  Mouse_Proctection = Resistor [tolerance=±5% resistance=220 package=THT]
  PNP = PNP-Transistor [package="TO92 [THT]"]
  Protection = Resistor [tolerance=±2% resistance=470 package=THT]

nets:
  GND: PC.-, EEGDC1.Pin_1, Mouse.Pin_3, Mouse.Pin_4, Mouse_Proctection.Pin_1, PNP.E
  N1: PC.+, Mouse_Proctection.Pin_0
  N2: EEGDC1.Pin_0, Protection.Pin_1
  N3: Mouse.Pin_2, PNP.B
  N4: PNP.C, Protection.Pin_0
